// Logisim project MainCircuit.circ as structural Verilog: 2 circuits, main circuit main
module main (
  output [3:0] out_1,
  output [3:0] out_2,
  output [3:0] out_3,
  output [3:0] out_4,
  output [3:0] out_5,
  output [3:0] out_6
);

  wire and_1_out, and_2_out, and_3_out, and_4_out, and_5_out, and_6_out, clock_1_out, j_k_ff_1_qn,
       j_k_ff_2_qn, j_k_ff_3_qn, j_k_ff_4_qn, j_k_ff_5_qn, j_k_ff_7_qn, j_k_ff_8_qn, j_k_ff_9_qn,
       j_k_ff_10_qn, j_k_ff_11_qn, j_k_ff_12_qn, j_k_ff_13_qn, j_k_ff_14_qn, j_k_ff_15_qn, j_k_ff_16_qn,
       j_k_ff_17_qn, j_k_ff_18_qn, j_k_ff_19_qn, j_k_ff_20_qn, n7_segment_display_driver_1_p5,
       n7_segment_display_driver_1_p6, n7_segment_display_driver_1_p7, n7_segment_display_driver_1_p8,
       n7_segment_display_driver_1_p9, n7_segment_display_driver_1_p10, n7_segment_display_driver_1_p11,
       n7_segment_display_driver_2_p5, n7_segment_display_driver_2_p6, n7_segment_display_driver_2_p7,
       n7_segment_display_driver_2_p8, n7_segment_display_driver_2_p9, n7_segment_display_driver_2_p10,
       n7_segment_display_driver_2_p11, n7_segment_display_driver_3_p5, n7_segment_display_driver_3_p6,
       n7_segment_display_driver_3_p7, n7_segment_display_driver_3_p8, n7_segment_display_driver_3_p9,
       n7_segment_display_driver_3_p10, n7_segment_display_driver_3_p11, n7_segment_display_driver_4_p5,
       n7_segment_display_driver_4_p6, n7_segment_display_driver_4_p7, n7_segment_display_driver_4_p8,
       n7_segment_display_driver_4_p9, n7_segment_display_driver_4_p10, n7_segment_display_driver_4_p11,
       n7_segment_display_driver_5_p5, n7_segment_display_driver_5_p6, n7_segment_display_driver_5_p7,
       n7_segment_display_driver_5_p8, n7_segment_display_driver_5_p9, n7_segment_display_driver_5_p10,
       n7_segment_display_driver_5_p11, n7_segment_display_driver_6_p5, n7_segment_display_driver_6_p6,
       n7_segment_display_driver_6_p7, n7_segment_display_driver_6_p8, n7_segment_display_driver_6_p9,
       n7_segment_display_driver_6_p10, n7_segment_display_driver_6_p11;

  J_K_Flip_Flop j_k_ff_1 (
    .J(1'b1), .clk(j_k_ff_13_qn), .K(1'b1), .Q(out_2[0]), .Qn(j_k_ff_1_qn), .reset(and_1_out));  // open: preset, en
  J_K_Flip_Flop j_k_ff_2 (
    .J(1'b1), .clk(j_k_ff_5_qn), .K(1'b1), .Q(out_1[0]), .Qn(j_k_ff_2_qn), .reset(and_2_out));  // open: preset, en
  J_K_Flip_Flop j_k_ff_3 (
    .J(1'b1), .clk(j_k_ff_1_qn), .K(1'b1), .Q(out_2[1]), .Qn(j_k_ff_3_qn), .reset(and_1_out));  // open: preset, en
  J_K_Flip_Flop j_k_ff_4 (
    .J(1'b1), .clk(j_k_ff_3_qn), .K(1'b1), .Q(out_2[2]), .Qn(j_k_ff_4_qn), .reset(and_1_out));  // open: preset, en
  J_K_Flip_Flop j_k_ff_5 (
    .J(1'b1), .clk(j_k_ff_4_qn), .K(1'b1), .Q(out_2[3]), .Qn(j_k_ff_5_qn), .reset(and_1_out));  // open: preset, en
  // _7_segment_display_driver 7_segment_display_driver_1: pin names not known; wires that end beside it: 1'b0, 1'b0, out_1[1], out_1[0], n7_segment_display_driver_1_p5, n7_segment_display_driver_1_p6, n7_segment_display_driver_1_p7, n7_segment_display_driver_1_p8, n7_segment_display_driver_1_p9, n7_segment_display_driver_1_p10, n7_segment_display_driver_1_p11
  and and_1 (and_1_out, j_k_ff_1_qn, out_2[1], j_k_ff_4_qn, out_2[3]);
  and and_2 (and_2_out, out_1[0], out_1[1]);
  J_K_Flip_Flop j_k_ff_6 (
    .J(1'b1), .clk(j_k_ff_2_qn), .K(1'b1), .Q(out_1[1]), .reset(and_2_out));  // open: Qn, preset, en
  // _7_segment_display_driver 7_segment_display_driver_2: pin names not known; wires that end beside it: out_2[3], out_2[2], out_2[1], out_2[0], n7_segment_display_driver_2_p5, n7_segment_display_driver_2_p6, n7_segment_display_driver_2_p7, n7_segment_display_driver_2_p8, n7_segment_display_driver_2_p9, n7_segment_display_driver_2_p10, n7_segment_display_driver_2_p11
  J_K_Flip_Flop j_k_ff_7 (
    .J(1'b1), .clk(j_k_ff_20_qn), .K(1'b1), .Q(out_4[0]), .Qn(j_k_ff_7_qn), .reset(and_3_out));  // open: preset, en
  _7_Segment_Display u_7_segment_display_1 (
    .g(n7_segment_display_driver_1_p11), .f(n7_segment_display_driver_1_p10),
    .a(n7_segment_display_driver_1_p5), .b(n7_segment_display_driver_1_p6),
    .e(n7_segment_display_driver_1_p9), .d(n7_segment_display_driver_1_p8), .c(n7_segment_display_driver_1_p7));  // open: dp
  J_K_Flip_Flop j_k_ff_8 (
    .J(1'b1), .clk(j_k_ff_7_qn), .K(1'b1), .Q(out_4[1]), .Qn(j_k_ff_8_qn), .reset(and_3_out));  // open: preset, en
  J_K_Flip_Flop j_k_ff_9 (
    .J(1'b1), .clk(j_k_ff_12_qn), .K(1'b1), .Q(out_3[0]), .Qn(j_k_ff_9_qn), .reset(and_4_out));  // open: preset, en
  _7_Segment_Display u_7_segment_display_2 (
    .g(n7_segment_display_driver_2_p11), .f(n7_segment_display_driver_2_p10),
    .a(n7_segment_display_driver_2_p5), .b(n7_segment_display_driver_2_p6),
    .e(n7_segment_display_driver_2_p9), .d(n7_segment_display_driver_2_p8), .c(n7_segment_display_driver_2_p7));  // open: dp
  J_K_Flip_Flop j_k_ff_10 (
    .J(1'b1), .clk(j_k_ff_8_qn), .K(1'b1), .Q(out_4[2]), .Qn(j_k_ff_10_qn), .reset(and_3_out));  // open: preset, en
  J_K_Flip_Flop j_k_ff_11 (
    .J(1'b1), .clk(j_k_ff_9_qn), .K(1'b1), .Q(out_3[1]), .Qn(j_k_ff_11_qn), .reset(and_4_out));  // open: preset, en
  J_K_Flip_Flop j_k_ff_12 (
    .J(1'b1), .clk(j_k_ff_10_qn), .K(1'b1), .Q(out_4[3]), .Qn(j_k_ff_12_qn), .reset(and_3_out));  // open: preset, en
  and and_3 (and_3_out, j_k_ff_7_qn, out_4[1], j_k_ff_10_qn, out_4[3]);
  and and_4 (and_4_out, j_k_ff_9_qn, out_3[1], out_3[2]);
  J_K_Flip_Flop j_k_ff_13 (
    .J(1'b1), .clk(j_k_ff_11_qn), .K(1'b1), .Q(out_3[2]), .Qn(j_k_ff_13_qn), .reset(and_4_out));  // open: preset, en
  // _7_segment_display_driver 7_segment_display_driver_3: pin names not known; wires that end beside it: 1'b0, out_3[2], out_3[1], out_3[0], n7_segment_display_driver_3_p5, n7_segment_display_driver_3_p6, n7_segment_display_driver_3_p7, n7_segment_display_driver_3_p8, n7_segment_display_driver_3_p9, n7_segment_display_driver_3_p10, n7_segment_display_driver_3_p11
  _7_Segment_Display u_7_segment_display_3 (
    .g(n7_segment_display_driver_3_p11), .f(n7_segment_display_driver_3_p10),
    .a(n7_segment_display_driver_3_p5), .b(n7_segment_display_driver_3_p6),
    .e(n7_segment_display_driver_3_p9), .d(n7_segment_display_driver_3_p8), .c(n7_segment_display_driver_3_p7));  // open: dp
  // _7_segment_display_driver 7_segment_display_driver_4: pin names not known; wires that end beside it: out_4[3], out_4[2], out_4[1], out_4[0], n7_segment_display_driver_4_p5, n7_segment_display_driver_4_p6, n7_segment_display_driver_4_p7, n7_segment_display_driver_4_p8, n7_segment_display_driver_4_p9, n7_segment_display_driver_4_p10, n7_segment_display_driver_4_p11
  _7_Segment_Display u_7_segment_display_4 (
    .g(n7_segment_display_driver_4_p11), .f(n7_segment_display_driver_4_p10),
    .a(n7_segment_display_driver_4_p5), .b(n7_segment_display_driver_4_p6),
    .e(n7_segment_display_driver_4_p9), .d(n7_segment_display_driver_4_p8), .c(n7_segment_display_driver_4_p7));  // open: dp
  J_K_Flip_Flop j_k_ff_14 (
    .J(1'b1), .clk(clock_1_out), .K(1'b1), .Q(out_5[0]), .Qn(j_k_ff_14_qn), .reset(and_5_out));  // open: preset, en
  J_K_Flip_Flop j_k_ff_15 (
    .J(1'b1), .clk(j_k_ff_14_qn), .K(1'b1), .Q(out_5[1]), .Qn(j_k_ff_15_qn), .reset(and_5_out));  // open: preset, en
  Clock clock_1 (.out(clock_1_out));
  J_K_Flip_Flop j_k_ff_16 (
    .J(1'b1), .clk(j_k_ff_19_qn), .K(1'b1), .Q(out_6[0]), .Qn(j_k_ff_16_qn), .reset(and_6_out));  // open: preset, en
  // _7_segment_display_driver 7_segment_display_driver_5: pin names not known; wires that end beside it: 1'b0, out_6[2], out_6[1], out_6[0], n7_segment_display_driver_5_p5, n7_segment_display_driver_5_p6, n7_segment_display_driver_5_p7, n7_segment_display_driver_5_p8, n7_segment_display_driver_5_p9, n7_segment_display_driver_5_p10, n7_segment_display_driver_5_p11
  J_K_Flip_Flop j_k_ff_17 (
    .J(1'b1), .clk(j_k_ff_15_qn), .K(1'b1), .Q(out_5[2]), .Qn(j_k_ff_17_qn), .reset(and_5_out));  // open: preset, en
  J_K_Flip_Flop j_k_ff_18 (
    .J(1'b1), .clk(j_k_ff_16_qn), .K(1'b1), .Q(out_6[1]), .Qn(j_k_ff_18_qn), .reset(and_6_out));  // open: preset, en
  _7_Segment_Display u_7_segment_display_5 (
    .g(n7_segment_display_driver_5_p11), .f(n7_segment_display_driver_5_p10),
    .a(n7_segment_display_driver_5_p5), .b(n7_segment_display_driver_5_p6),
    .e(n7_segment_display_driver_5_p9), .d(n7_segment_display_driver_5_p8), .c(n7_segment_display_driver_5_p7));  // open: dp
  and and_5 (and_5_out, j_k_ff_14_qn, out_5[1], j_k_ff_17_qn, out_5[3]);
  J_K_Flip_Flop j_k_ff_19 (
    .J(1'b1), .clk(j_k_ff_17_qn), .K(1'b1), .Q(out_5[3]), .Qn(j_k_ff_19_qn), .reset(and_5_out));  // open: preset, en
  and and_6 (and_6_out, j_k_ff_16_qn, out_6[1], out_6[2]);
  J_K_Flip_Flop j_k_ff_20 (
    .J(1'b1), .clk(j_k_ff_18_qn), .K(1'b1), .Q(out_6[2]), .Qn(j_k_ff_20_qn), .reset(and_6_out));  // open: preset, en
  // _7_segment_display_driver 7_segment_display_driver_6: pin names not known; wires that end beside it: out_5[3], out_5[2], out_5[1], out_5[0], n7_segment_display_driver_6_p5, n7_segment_display_driver_6_p6, n7_segment_display_driver_6_p7, n7_segment_display_driver_6_p8, n7_segment_display_driver_6_p9, n7_segment_display_driver_6_p10, n7_segment_display_driver_6_p11
  _7_Segment_Display u_7_segment_display_6 (
    .g(n7_segment_display_driver_6_p11), .f(n7_segment_display_driver_6_p10),
    .a(n7_segment_display_driver_6_p5), .b(n7_segment_display_driver_6_p6),
    .e(n7_segment_display_driver_6_p9), .d(n7_segment_display_driver_6_p8), .c(n7_segment_display_driver_6_p7));  // open: dp

  assign out_1[3:2] = 2'b00;
  assign out_3[3] = 1'b0;
  assign out_6[3] = 1'b0;

  // Notes on the sheet:
  //   mod 24 to count hours
  //   mod 60 implemented by mod 10 for units place and mod 3 for tens place
  //   mod 60 to count minutes
  //   mod 60 implemented by mod 10 for units place and mod 6 for tens place
  //   mod 60 to count seconds
  //   mod 60 implemented by mod 10 for units place and mod 6 for tens place
  //   1Hz Clock
  //   Constant 1 supplied to J and K inputs of all flip-flops
  //   1Hz frequency is supplied to first flip flop of unit place of second counter
  //   The next flip flop operates at half the frequency of the previous flip-flop, which can also be explained as
  //   the frequency of the previous wave's falling edge.
  //   Ground for uniform 4 bit output
endmodule

module BCDto7Segment (
  input  D,
  input  C,
  input  B,
  input  A,
  output a_2,
  output b_2,
  output c_2,
  output d_2,
  output e,
  output f,
  output g
);

  wire nand_1_out, nand_2_out, nand_3_out, nand_4_out, nand_5_out, nand_6_out, nand_7_out, nand_8_out,
       nand_9_out, nand_10_out, nand_11_out, nand_12_out, nand_13_out, nand_14_out, nand_15_out, nand_16_out,
       nand_17_out, nand_18_out, nand_19_out, nand_20_out, nand_21_out, nand_22_out, nand_23_out,
       nand_24_out, nand_25_out, nand_26_out, nand_27_out, nand_28_out, nand_29_out, nand_30_out,
       nand_31_out, nand_32_out, nand_33_out, nand_34_out, nand_35_out, nand_36_out, nand_37_out,
       nand_38_out, nand_39_out, nand_40_out, nand_41_out, nand_42_out, nand_43_out, nand_44_out,
       nand_45_out, nand_46_out, nand_47_out, nand_48_out, nand_49_out, nand_50_out, nand_51_out,
       nand_52_out, nand_53_out, nand_54_out, nand_55_out, nand_56_out, nand_57_out, nand_58_out,
       nand_59_out, nand_60_out, nand_61_out, nand_62_out, nand_63_out, nand_64_out, nand_65_out,
       nand_66_out, nand_67_out, nand_68_out, nand_69_out, nand_70_out, nand_71_out, nand_72_out,
       nand_73_out, nand_74_out, nand_75_out, nand_76_out, nand_77_out, nand_78_out, nand_79_out,
       nand_80_out, nand_81_out, nand_82_out, nand_83_out, nand_84_out, nand_85_out, nand_86_out,
       nand_87_out, nand_88_out, nand_89_out, nand_90_out, nand_91_out, nand_92_out, nand_93_out,
       nand_94_out, nand_95_out, nand_96_out, nand_97_out, nand_98_out, nand_99_out, nand_100_out,
       nand_101_out, nand_102_out, nand_103_out, nand_104_out, nand_106_out, nand_107_out, nand_108_out,
       nand_109_out, nand_110_out, nand_111_out, nand_112_out, nand_113_out, nand_114_out, nand_115_out,
       nand_116_out, nand_117_out, nand_118_out, nand_119_out, nand_120_out, nand_121_out, nand_122_out,
       nand_123_out, nand_124_out, nand_125_out, nand_126_out, nand_127_out, nand_128_out, nand_129_out,
       nand_130_out, nand_131_out, nand_132_out, nand_133_out, nand_134_out, nand_136_out, nand_137_out,
       nand_138_out, nand_139_out, nand_141_out, nand_142_out, nand_143_out, nand_144_out, nand_145_out,
       nand_146_out, nand_147_out, nand_148_out;

  nand nand_1 (nand_1_out, C, C);
  nand nand_2 (nand_2_out, D, D);
  nand nand_3 (nand_3_out, B, B);
  nand nand_4 (nand_4_out, D, D);
  nand nand_5 (nand_5_out, B, B);
  nand nand_6 (nand_6_out, D, D);
  nand nand_7 (nand_7_out, D, D);
  nand nand_8 (nand_8_out, C, C);
  nand nand_9 (nand_9_out, C, C);
  nand nand_10 (nand_10_out, C, C);
  nand nand_11 (nand_11_out, A, A);
  nand nand_12 (nand_12_out, A, A);
  nand nand_13 (nand_13_out, D, D);
  nand nand_14 (nand_14_out, C, C);
  nand nand_15 (nand_15_out, A, A);
  nand nand_16 (nand_16_out, D, D);
  nand nand_17 (nand_17_out, D, nand_1_out);
  nand nand_18 (nand_18_out, nand_2_out, nand_3_out);
  nand nand_19 (nand_19_out, nand_4_out, nand_5_out);
  nand nand_20 (nand_20_out, nand_6_out, A);
  nand nand_21 (nand_21_out, nand_7_out, nand_8_out);
  nand nand_22 (nand_22_out, nand_9_out, B);
  nand nand_23 (nand_23_out, nand_10_out, nand_11_out);
  nand nand_24 (nand_24_out, B, nand_12_out);
  nand nand_25 (nand_25_out, D, B);
  nand nand_26 (nand_26_out, D, C);
  nand nand_27 (nand_27_out, nand_13_out, C);
  nand nand_28 (nand_28_out, nand_14_out, B);
  nand nand_29 (nand_29_out, B, nand_15_out);
  nand nand_30 (nand_30_out, nand_16_out, C);
  nand nand_31 (nand_31_out, C, C);
  nand nand_32 (nand_32_out, A, A);
  nand nand_33 (nand_33_out, D, D);
  nand nand_34 (nand_34_out, D, D);
  nand nand_35 (nand_35_out, nand_17_out, nand_17_out);
  nand nand_36 (nand_36_out, B, B);
  nand nand_37 (nand_37_out, D, D);
  nand nand_38 (nand_38_out, C, C);
  nand nand_39 (nand_39_out, nand_18_out, nand_18_out);
  nand nand_40 (nand_40_out, A, A);
  nand nand_41 (nand_41_out, D, D);
  nand nand_42 (nand_42_out, B, B);
  nand nand_43 (nand_43_out, nand_19_out, nand_20_out);
  nand nand_44 (nand_44_out, B, B);
  nand nand_45 (nand_45_out, D, D);
  nand nand_46 (nand_46_out, C, C);
  nand nand_47 (nand_47_out, nand_21_out, nand_21_out);
  nand nand_48 (nand_48_out, A, A);
  nand nand_49 (nand_49_out, nand_22_out, nand_22_out);
  nand nand_50 (nand_50_out, B, B);
  nand nand_51 (nand_51_out, B, B);
  nand nand_52 (nand_52_out, nand_23_out, nand_24_out);
  nand nand_53 (nand_53_out, nand_25_out, nand_26_out);
  nand nand_54 (nand_54_out, B, B);
  nand nand_55 (nand_55_out, A, A);
  nand nand_56 (nand_56_out, nand_27_out, nand_27_out);
  nand nand_57 (nand_57_out, B, B);
  nand nand_58 (nand_58_out, nand_28_out, nand_29_out);
  nand nand_59 (nand_59_out, nand_30_out, nand_30_out);
  nand nand_60 (nand_60_out, B, B);
  nand nand_61 (nand_61_out, C, C);
  nand nand_62 (nand_62_out, nand_31_out, nand_32_out);
  nand nand_63 (nand_63_out, nand_33_out, B);
  nand nand_64 (nand_64_out, nand_34_out, C);
  nand nand_65 (nand_65_out, C, B);
  nand nand_66 (nand_66_out, nand_35_out, nand_36_out);
  nand nand_67 (nand_67_out, nand_37_out, nand_38_out);
  nand nand_68 (nand_68_out, nand_39_out, nand_40_out);
  nand nand_69 (nand_69_out, nand_41_out, B);
  nand nand_70 (nand_70_out, D, nand_42_out);
  nand nand_71 (nand_71_out, nand_43_out, nand_43_out);
  nand nand_72 (nand_72_out, nand_44_out, A);
  nand nand_73 (nand_73_out, nand_45_out, C);
  nand nand_74 (nand_74_out, D, nand_46_out);
  nand nand_75 (nand_75_out, nand_47_out, nand_48_out);
  nand nand_76 (nand_76_out, nand_49_out, A);
  nand nand_77 (nand_77_out, C, nand_50_out);
  nand nand_78 (nand_78_out, C, B);
  nand nand_79 (nand_79_out, D, nand_51_out);
  nand nand_80 (nand_80_out, nand_52_out, nand_52_out);
  nand nand_81 (nand_81_out, nand_53_out, nand_53_out);
  nand nand_82 (nand_82_out, nand_54_out, nand_55_out);
  nand nand_83 (nand_83_out, nand_56_out, nand_57_out);
  nand nand_84 (nand_84_out, nand_58_out, nand_58_out);
  nand nand_85 (nand_85_out, nand_59_out, nand_60_out);
  nand nand_86 (nand_86_out, D, nand_61_out);
  nand nand_87 (nand_87_out, D, A);
  nand nand_88 (nand_88_out, nand_62_out, nand_63_out);
  nand nand_89 (nand_89_out, nand_64_out, nand_64_out);
  nand nand_90 (nand_90_out, nand_65_out, nand_66_out);
  nand nand_91 (nand_91_out, A, A);
  nand nand_92 (nand_92_out, nand_67_out, nand_68_out);
  nand nand_93 (nand_93_out, C, C);
  nand nand_94 (nand_94_out, A, A);
  nand nand_95 (nand_95_out, nand_69_out, nand_69_out);
  nand nand_96 (nand_96_out, nand_70_out, nand_70_out);
  nand nand_97 (nand_97_out, nand_71_out, nand_72_out);
  nand nand_98 (nand_98_out, nand_73_out, nand_74_out);
  nand nand_99 (nand_99_out, nand_75_out, nand_76_out);
  nand nand_100 (nand_100_out, nand_77_out, nand_77_out);
  nand nand_101 (nand_101_out, nand_78_out, nand_78_out);
  nand nand_102 (nand_102_out, A, A);
  nand nand_103 (nand_103_out, nand_79_out, nand_79_out);
  nand nand_104 (nand_104_out, A, A);
  nand nand_105 (e, nand_80_out, nand_81_out);
  nand nand_106 (nand_106_out, nand_82_out, nand_83_out);
  nand nand_107 (nand_107_out, A, A);
  nand nand_108 (nand_108_out, C, C);
  nand nand_109 (nand_109_out, nand_84_out, nand_85_out);
  nand nand_110 (nand_110_out, nand_86_out, nand_87_out);
  nand nand_111 (nand_111_out, nand_88_out, nand_88_out);
  nand nand_112 (nand_112_out, nand_89_out, A);
  nand nand_113 (nand_113_out, nand_90_out, nand_90_out);
  nand nand_114 (nand_114_out, D, nand_91_out);
  nand nand_115 (nand_115_out, nand_92_out, nand_92_out);
  nand nand_116 (nand_116_out, nand_93_out, nand_94_out);
  nand nand_117 (nand_117_out, nand_95_out, A);
  nand nand_118 (nand_118_out, nand_96_out, A);
  nand nand_119 (nand_119_out, nand_97_out, nand_97_out);
  nand nand_120 (nand_120_out, nand_98_out, nand_98_out);
  nand nand_121 (nand_121_out, nand_99_out, nand_99_out);
  nand nand_122 (nand_122_out, nand_100_out, A);
  nand nand_123 (nand_123_out, nand_101_out, nand_102_out);
  nand nand_124 (nand_124_out, nand_103_out, nand_104_out);
  nand nand_125 (nand_125_out, nand_106_out, nand_106_out);
  nand nand_126 (nand_126_out, C, nand_107_out);
  nand nand_127 (nand_127_out, D, nand_108_out);
  nand nand_128 (nand_128_out, D, B);
  nand nand_129 (nand_129_out, nand_109_out, nand_109_out);
  nand nand_130 (nand_130_out, nand_110_out, nand_110_out);
  nand nand_131 (nand_131_out, nand_111_out, nand_112_out);
  nand nand_132 (nand_132_out, nand_113_out, nand_114_out);
  nand nand_133 (nand_133_out, nand_115_out, nand_116_out);
  nand nand_134 (nand_134_out, nand_117_out, nand_118_out);
  nand nand_135 (c_2, nand_119_out, nand_120_out);
  nand nand_136 (nand_136_out, nand_121_out, nand_122_out);
  nand nand_137 (nand_137_out, nand_123_out, nand_124_out);
  nand nand_138 (nand_138_out, nand_125_out, nand_126_out);
  nand nand_139 (nand_139_out, nand_127_out, nand_128_out);
  nand nand_140 (g, nand_129_out, nand_130_out);
  nand nand_141 (nand_141_out, nand_131_out, nand_131_out);
  nand nand_142 (nand_142_out, nand_132_out, nand_132_out);
  nand nand_143 (nand_143_out, nand_133_out, nand_133_out);
  nand nand_144 (nand_144_out, nand_134_out, nand_134_out);
  nand nand_145 (nand_145_out, nand_136_out, nand_136_out);
  nand nand_146 (nand_146_out, nand_137_out, nand_137_out);
  nand nand_147 (nand_147_out, nand_138_out, nand_138_out);
  nand nand_148 (nand_148_out, nand_139_out, nand_139_out);
  nand nand_149 (a_2, nand_141_out, nand_142_out);
  nand nand_150 (b_2, nand_143_out, nand_144_out);
  nand nand_151 (d_2, nand_145_out, nand_146_out);
  nand nand_152 (f, nand_147_out, nand_148_out);
endmodule
